# Fritzing sketch dc-light-box (saved by Fritzing 0.9.3b)

parts:
  U1 = NodeMCU V3.0
  U2 = Optocoupler [package=THT]
  R1 = Resistor [tolerance=±5% resistance=1k package="2512 [SMD]"]
  VCC2 = 4 x AAA Battery Mount
  LED1 = LED - 5mm [color="Red (633nm)" package="5 mm [THT]"]
  U4 = XL4001 LED driver module
  LED2 = LED - 5mm [color="Red (633nm)" package="5 mm [THT]"]
  LED3 = LED - 5mm [color="Red (633nm)" package="5 mm [THT]"]
  LED4 = LED - 5mm [color="Red (633nm)" package="5 mm [THT]"]
  LED5 = LED - 5mm [color="Red (633nm)" package="5 mm [THT]"]
  LED6 = LED - 5mm [color="Red (633nm)" package="5 mm [THT]"]
  Grove1 = Grove - SPDT Relay(30A) [part_number=103020012]

nets:
  N1: U1.D1, Grove1.SIG
  3V3: U1.3V3, Grove1.VCC
  GND: U1.GND, U2.Pin_2, VCC2.-, Grove1.GND
  N2: U1.D5, R1.Pin_1
  N3: U1.Vin, VCC2.+
  N4: U2.Pin_1, R1.Pin_0
  N5: U2.Pin_4, U4.VIN-, U4.GND
  N6: U2.Pin_5, U4.PWM
  N7: LED1.cathode, Grove1.RelayNO
  N8: LED1.anode, LED2.cathode
  N9: U4.OUT+, LED6.anode
  N10: U4.OUT-, Grove1.RelayCom
  N11: LED2.anode, LED3.cathode
  N12: LED3.anode, LED4.cathode
  N13: LED4.anode, LED5.cathode
  N14: LED5.anode, LED6.cathode

notes:
  This would be your Mean Well driver (HLG-185H-C700B in the BOM) where :
  LED - is Vo- in MW driver
  LED + is Vo+ in MW driver
  PWM is DIM+ in MW driver
  GND is DIM- in MW driver
  VIN - is ACN in MW driver
  VIN + is ACL in MW driver
  Note : the part in Fritzing does not have a connector for AC ground

custom parts:
  NodeMCU V3.0: ESP8266 based NodeMCU
  XL4001 LED driver module: XL4001 based LED driver module with PWM control
  Grove - SPDT Relay(30A): TheSPDT Relay(30A) is a high quality Single Pole Double Throw Relay(SPDT).The Relay consist of a coil, 1 common terminal, 1 normally closed(NC) terminal and one normally open(NO) terminal. When the coil of the relay is at rest (not energized), the common terminal and the normally closed terminal have continuity. When the coil is energized, the common terminal and the normally open terminal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
